# Fritzing sketch temp-box (saved by Fritzing 0.9.4)
circuit board: 8.46667cm x 5.64444cm
perfboards: 1

parts:
  R1 = Resistor [tolerance=±5% resistance=100k package=THT]
  Mod1 = Raspberry Pi Pico
  Grove1 = Grove OLED 128x96
  U1 = 2.5mm Audio Jack [package=stereojack2.5mm_smd]
  VCC1 = Battery
  D1 = Schottky Diode [part_number=1N5817 package="Melf DO-213 AB [SMD]"]

nets:
  N1: R1.Pin_0, Mod1.pin_34, U1.LEFT
  N2: R1.Pin_1, Mod1.pin_35, Mod1.pin_36, Grove1.VCC
  N3: Mod1.pin_3, Mod1.pin_8, Mod1.pin_13, Mod1.pin_18, Mod1.pin_23, Mod1.pin_28, Mod1.pin_33, Mod1.pin_38, Mod1.pin_42, Grove1.GND, U1.RIGHT, VCC1.-
  N4: Mod1.pin_11, Grove1.SDA
  N5: Mod1.pin_12, Grove1.SCL
  N6: Mod1.pin_39, D1.cathode
  N7: VCC1.+, D1.anode

custom parts:
  Raspberry Pi Pico: Raspberry Pi Pico. Based around the RP2040 microcontroller the Pico is a low cost microcontroller device bringing Raspberry Pi quality, cost, and easy of use to the microcontroller space. Jan 2021, Split part in to two versions: tht (this one) and SMD. This one will drill holes for a .1 in header in pcb to allow plugging in the module as well as providing pads to solder the module to the top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
